# Fritzing sketch ReadAnalogVoltage (saved by Fritzing 0.9.2b)
breadboards: 1

parts:
  Arduino_UNO = Arduino Uno (Rev3)
  R1 = Rotary Potentiometer (Small) [maximum_resistance=100kΩ package=THT]

nets:
  N1: Arduino_UNO.A0, R1.wiper
  N2: Arduino_UNO.5V, R1.leg2
  N3: Arduino_UNO.GND, R1.leg1
