# Fritzing sketch Blink (saved by Fritzing 0.9.2b)
breadboards: 1

parts:
  Arduino_UNO = Arduino Uno (Rev3)
  LED = LED - 5mm [color="Red (633nm)" package="5 mm [THT]"]
  part = Resistor [tolerance=±5% resistance=220 package=THT]

nets:
  N1: Arduino_UNO.D13/SCK, LED.anode
  N2: Arduino_UNO.GND, part.Pin_0
  N3: LED.cathode, part.Pin_1
