# Fritzing sketch DigitalInputPullup (saved by Fritzing 0.9.2b)
breadboards: 1

parts:
  Part1 = Arduino Uno (Rev3)
  Switch = Pushbutton [package=THT]

nets:
  N1: Part1.GND, Switch.leg1
  N2: Part1.D2, Switch.leg0
