# Fritzing sketch Button (saved by Fritzing 0.9.2b)
breadboards: 1

parts:
  Part1 = Arduino Uno (Rev3)
  S1 = Toggle Switch [package=THT]
  LED = LED - 5mm [color="Red (633nm)" package="5 mm [THT]"]
  part = Resistor [tolerance=±5% resistance=220 package=THT]

nets:
  N1: Part1.D13/SCK, LED.anode
  N2: Part1.GND, S1.L2, part.Pin_0
  N3: Part1.D2, S1.COM
  N4: Part1.5V, S1.L1
  N5: LED.cathode, part.Pin_1
