# Fritzing sketch BlinkwithoutDelay (saved by Fritzing 0.9.2b)
breadboards: 1

parts:
  Arduino_UNO = Arduino Uno (Rev3)
  LED = LED - 5mm [color="Red (633nm)" package="5 mm [THT]"]
  R1 = Resistor [tolerance=±5% resistance=220 package=THT]

nets:
  N1: Arduino_UNO.GND, LED.cathode
  N2: Arduino_UNO.5V, R1.Pin_1
  N3: LED.anode, R1.Pin_0
