# Fritzing sketch StateChangeDetection (saved by Fritzing 0.9.2b)
breadboards: 1

parts:
  Arduino_UNO = Arduino Uno (Rev3)
  Switch = Pushbutton [package=THT]
  part = Resistor [tolerance=±5% resistance=10k package=THT]
  LED = LED - 5mm [color="Red (633nm)" package="5 mm [THT]"]

nets:
  N1: Arduino_UNO.D13/SCK, LED.anode
  N2: Arduino_UNO.GND, part.Pin_0, LED.cathode
  N3: Arduino_UNO.D2, Switch.leg1, part.Pin_1
  N4: Arduino_UNO.5V, Switch.leg0
