# Fritzing sketch Debounce (saved by Fritzing 0.9.2b)
breadboards: 1

parts:
  Arduino_UNO = Arduino Uno (Rev3)
  LED = LED - 5mm [color="Red (633nm)" package="5 mm [THT]"]
  R1 = Resistor [tolerance=±5% resistance=220 package=THT]
  R2 = Resistor [tolerance=±5% resistance=10k package=THT]
  Switch = Pushbutton [package=THT]

nets:
  N1: Arduino_UNO.D13/SCK, R1.Pin_1
  N2: Arduino_UNO.D2, R2.Pin_0, Switch.leg0
  N3: Arduino_UNO.5V, Switch.leg1
  N4: Arduino_UNO.GND, LED.cathode, R2.Pin_1
  N5: LED.anode, R1.Pin_0
